// Logisim project EdgeComputer.circ as structural Verilog
module MicroCode (
  input  [11:0] STATE,
  output PRIVILEDGED,
  output LATCH_ADDR,
  output LATCH_FLAGS,
  output [2:0] ALU_OP,
  output [1:0] ALU_CARRY,
  output [1:0] ADDR_REG,
  output BUS_DIR,
  output BUS_BYTE,
  output MDR_SOURCE,
  output TLB_DISABLE,
  output [1:0] TLB_WRITE,
  output [3:0] L_BUS,
  output [1:0] R_BUS,
  output [2:0] Z_REG,
  output [2:0] Z_ADDR,
  output [3:0] IMMEDIATE,
  output FLAG_SOURCE,
  output [2:0] CONDITION,
  output [11:0] NEXT_STATE
);

  ROM #(.addrWidth(12), .dataWidth(16)) rom_1 (
    .addr(STATE),
    .data({TLB_WRITE, TLB_DISABLE, MDR_SOURCE, BUS_BYTE, BUS_DIR, ADDR_REG, ALU_CARRY, ALU_OP, LATCH_FLAGS, LATCH_ADDR, PRIVILEDGED}));  // open: sel
  ROM #(.addrWidth(12), .dataWidth(16)) rom_2 (
    .addr(STATE), .data({IMMEDIATE, Z_ADDR, Z_REG, R_BUS, L_BUS}));  // open: sel
  ROM #(.addrWidth(12), .dataWidth(16)) rom_3 (.addr(STATE), .data({NEXT_STATE, CONDITION, FLAG_SOURCE}));  // open: sel

  // Notes on the sheet:
  //   contents of rom_1 (hex, n*v repeats v):
  //   1702 4001 8001 c001 1402 1702 10 248*1702 400 1702 1702 1702 1902 c 1f02 1702 1702 2 1300 400 2 1300
  //   400 2 1300 3a 12 6 82 1702 3287*0 2 0 2 1300 2 1300 2 1300 2 0 2 0 2 0 2 0 2 0 2 0 2 0 2 0 2 0 2 0 2
  //   0 2 0 2 0 2 0 2 0 2 0 2 0 2 0 2 0 2 0 2 0 2 0 2 0 2 0 2 0 2 0 2 0 2 0 2 0 2 0 2 0 2 0 2 0 2 0 2 0 2
  //   0 2 0 2 0 2 0 2 0 2 0 2 0 2 0 2 0 2 0 2 0 2 0 2 0 2 0 2 0 2 0 2 0 2 0 2 0 2 0 2 0 2 0 2 0 2 0 2 0 2
  //   0 2 0 2 0 2 0 2 0 2 0 2 0 2 0 2 0 2 0 2 0 2 0 2 0 2 0 2 0 2 0 2 0 2 0 2 0 2 0 2 0 2 0 2 0 2 0 2 0 2
  //   0 2 0 2 0 2 0 2 0 2 0 2 0 2 0 2 0 2 0 2 0 2 0 2 0 2 0 2 0 2 0 2 0 2 0 2 0 2 0 2 0 2 0 2 0 2 0 2 0 2
  //   0 2 0 2 0 2 0 2 0 2 0 2 0 2 0 2 0 2 0 2 0 2 0 2 0 2 0 2 0 2 0 2 0 2 0 2 0 2 0 2 0 2 0 2 0 2 0 2 0 2
  //   0 2 0 2 0 2 0 2 0 2 0 2 0 2 0 2 0 2 0 2 0 2 0 2 0 2 0 2 0 2 0 2 0 2 0 2 0 2 0 2 0 2 0 2 0 2 0 2 0 2
  //   0 2 0 2 0 2 0 2 0 2 0 2 0 2 0 2 0 2 0 2 0 2 0 2 0 2 0 2 0 2 0 2 0 2 0 2 0 2 0 2 0 2 0 2 0 2 0 2 0 2
  //   0 2 0 2 0 2 0 2 0 2 0 2 0 2 0 2 0 2 0 2 0 2 0 2 0 2 0 2 0 2 0 2 0 2 0 2 0 2 0 2 0 2 0 2 0 2 0 2 0 2
  //   0 2 0 2 0 2 0 2 0 2 0 2 0 2 0 2 0 2 0 2 0 2 0 2 0 2 0 2 0 2 0 2 0 2 0 2 0 2 0 2 0 2 0 2 0 2 0 2 0 2
  //   0 2 0 2 0 2 0 2 0 2 0 2 0 2 0 2 0 2 0 2 0 2 0 2 0 2 0 2 1702 2 0 2 1702 2 0 2 1f02 2 0 1702 1402 2 c
  //   2 1902 2 0 2 0 2 0 2
  //   contents of rom_2 (hex, n*v repeats v):
  //   161b 2 2 2 1018 161b 51 248*161b 1 161b 161b 161b 1219 1052 161b 161b 161b 141a 0 b 141a 0 f 141a 0
  //   607 761b 63b e17 161b 3287*0 1e1f 0 1c1e 0 1c1e 0 1c1e 0 1e1f 0 1e1f 0 1e1f 0 1e1f 0 1e1f 0 1e1f 0
  //   1e1f 0 1e1f 0 1e1f 0 1e1f 0 1e1f 0 1e1f 0 1e1f 0 1e1f 0 1e1f 0 1e1f 0 1e1f 0 1e1f 0 1e1f 0 1e1f 0
  //   1e1f 0 1e1f 0 1e1f 0 1e1f 0 1e1f 0 1e1f 0 1e1f 0 1e1f 0 1e1f 0 1e1f 0 1e1f 0 1e1f 0 1e1f 0 1e1f 0
  //   1e1f 0 1e1f 0 1e1f 0 1e1f 0 1e1f 0 1e1f 0 1e1f 0 1e1f 0 1e1f 0 1e1f 0 1e1f 0 1e1f 0 1e1f 0 1e1f 0
  //   1e1f 0 1e1f 0 1e1f 0 1e1f 0 1e1f 0 1e1f 0 1e1f 0 1e1f 0 1e1f 0 1e1f 0 1e1f 0 1e1f 0 1e1f 0 1e1f 0
  //   1e1f 0 1e1f 0 1e1f 0 1e1f 0 1e1f 0 1e1f 0 1e1f 0 1e1f 0 1e1f 0 1e1f 0 1e1f 0 1e1f 0 1e1f 0 1e1f 0
  //   1e1f 0 1e1f 0 1e1f 0 1e1f 0 1e1f 0 1e1f 0 1e1f 0 1e1f 0 1e1f 0 1e1f 0 1e1f 0 1e1f 0 1e1f 0 1e1f 0
  //   1e1f 0 1e1f 0 1e1f 0 1e1f 0 1e1f 0 1e1f 0 1e1f 0 1e1f 0 1e1f 0 1e1f 0 1e1f 0 1e1f 0 1e1f 0 1e1f 0
  //   1e1f 0 1e1f 0 1e1f 0 1e1f 0 1e1f 0 1e1f 0 1e1f 0 1e1f 0 1e1f 0 1e1f 0 1e1f 0 1e1f 0 1e1f 0 1e1f 0
  //   1e1f 0 1e1f 0 1e1f 0 1e1f 0 1e1f 0 1e1f 0 1e1f 0 1e1f 0 1e1f 0 1e1f 0 1e1f 0 1e1f 0 1e1f 0 1e1f 0
  //   1e1f 0 1e1f 0 1e1f 0 1e1f 0 1e1f 0 1e1f 0 1e1f 0 1e1f 0 1e1f 0 1e1f 0 1e1f 0 1e1f 0 1e1f 0 1e1f 0
  //   1e1f 0 1e1f 0 1e1f 0 1e1f 0 1e1f 0 1e1f 0 1e1f 0 1e1f 0 1e1f 0 1e1f 0 1e1f 0 1e1f 0 1e1f 0 1e1f 0
  //   1e1f 0 1e1f 0 1e1f 0 1e1f 0 1e1f 0 1e1f 0 1e1f 0 1e1f 0 1e1f 0 1e1f 0 1e1f 0 1e1f 0 1e1f 0 1e1f 0
  //   1e1f 0 1e1f 0 1e1f 0 1e1f 0 1e1f 0 1e1f 0 1e1f 0 1e1f 0 1e1f 0 1e1f 0 1e1f 0 1e1f 0 1e1f 0 1e1f 0
  //   1e1f 0 1e1f 0 1e1f 0 1e1f 0 1e1f 0 1e1f 0 1e1f 0 1e1f 0 1e1f 0 1e1f 0 1e1f 0 1e1f 0 1e1f 0 1e1f 0
  //   1e1f 0 1e1f 0 1e1f 0 1e1f 0 1e1f 0 1e1f 0 1e1f 0 1e1f 0 1e1f 0 1e1f 0 1e1f 0 1e1f 0 1e1f 0 1e1f 0
  //   1e1f 0 1e1f 0 1e1f 0 1e1f 0 1e1f 0 1e1f 0 1e1f 0 1e1f 0 1e1f 0 1e1f 0 1e1f 0 1e1f 0 1e1f 0 1e1f 0
  //   1e1f 0 1e1f 0 1e1f 0 1e1f 0 1e1f 0 1e1f 0 1e1f 0 1e1f 0 1e1f 0 1e1f 0 1e1f 0 1e1f 0 1e1f 0 1e1f 0
  //   1e1f 0 1e1f 0 1e1f 0 1e1f 0 1e1f 0 e00 161b 1e1f 0 600 161b 1e1f 0 1e1f 161b 1e1f 0 161b 1018 1a1d
  //   1052 181c 1219 1e1f 0 1e1f 0 1e1f 0 1e1f
  //   contents of rom_3 (hex, n*v repeats v):
  //   ffe9 1000 1010 1020 ff69 fee9 0 fe29 fe09 fde9 fdc9 fda9 fd89 fd69 fd49 fd29 fd09 fce9 fcc9 fca9
  //   fc89 fc69 fc49 fc29 fc09 fbe9 fbc9 fba9 fb89 fb69 fb49 fb29 fb09 fae9 fac9 faa9 fa89 fa69 fa49 fa29
  //   fa09 f9e9 f9c9 f9a9 f989 f969 f949 f929 f909 f8e9 f8c9 f8a9 f889 f869 f849 f829 f809 f7e9 f7c9 f7a9
  //   f789 f769 f749 f729 f709 f6e9 f6c9 f6a9 f689 f669 f649 f629 f609 f5e9 f5c9 f5a9 f589 f569 f549 f529
  //   f509 f4e9 f4c9 f4a9 f489 f469 f449 f429 f409 f3e9 f3c9 f3a9 f389 f369 f349 f329 f309 f2e9 f2c9 f2a9
  //   f289 f269 f249 f229 f209 f1e9 f1c9 f1a9 f189 f169 f149 f129 f109 f0e9 f0c9 f0a9 f089 f069 f049 f029
  //   f009 efe9 efc9 efa9 ef89 ef69 ef49 ef29 ef09 eee9 eec9 eea9 ee89 ee69 ee49 ee29 ee09 ede9 edc9 eda9
  //   ed89 ed69 ed49 ed29 ed09 ece9 ecc9 eca9 ec89 ec69 ec49 ec29 ec09 ebe9 ebc9 eba9 eb89 eb69 eb49 eb29
  //   eb09 eae9 eac9 eaa9 ea89 ea69 ea49 ea29 ea09 e9e9 e9c9 e9a9 e989 e969 e949 e929 e909 e8e9 e8c9 e8a9
  //   e889 e869 e849 e829 e809 e7e9 e7c9 e7a9 e789 e769 e749 e729 e709 e6e9 e6c9 e6a9 e689 e669 e649 e629
  //   e609 e5e9 e5c9 e5a9 e589 e569 e549 e529 e509 e4e9 e4c9 e4a9 e489 e469 e449 e429 e409 e3e9 e3c9 e3a9
  //   e389 e369 e349 e329 e309 e2e9 e2c9 e2a9 e289 e269 e249 e229 e209 e1e9 e1c9 e1a9 e189 e169 e149 e129
  //   e109 e0e9 e0c9 e0a9 e089 e069 e049 e029 e009 dfe9 dfc9 dfa9 df89 df69 df49 1080 ffc9 ffa9 ff89 ff49
  //   ff28 fec9 fe89 fe49 df29 10a0 10b0 df09 10d0 10e0 dee9 1100 1110 1120 1130 1140 dec9 3289*0 10f0
  //   1100 10c0 10d0 1090 10a0 498*0 1070 fe49 fe68 fe68 1060 fe89 fea8 fea8 1050 fec9 0 0 ff09 ff69 1040
  //   ff28 1030 ff49
endmodule

module Immediate (
  input  [3:0] IMM,
  output [15:0] I
);

  wire decoder_1_out0, decoder_1_out1, decoder_1_out2, decoder_1_out3, decoder_1_out4, decoder_1_out5,
       decoder_1_out6, decoder_1_out7, decoder_1_out8, decoder_1_out9, decoder_1_out10, decoder_1_out11,
       decoder_1_out13, decoder_1_out14, decoder_1_out15, or_1_out, or_2_out;

  Decoder #(.select(4), .disabled(0), .enable("false")) decoder_1 (
    .out0(decoder_1_out0), .out1(decoder_1_out1), .out2(decoder_1_out2), .out3(decoder_1_out3),
    .out4(decoder_1_out4), .out5(decoder_1_out5), .out6(decoder_1_out6), .out7(decoder_1_out7),
    .out8(decoder_1_out8), .out9(decoder_1_out9), .out10(decoder_1_out10), .out11(decoder_1_out11),
    .out13(decoder_1_out13), .out14(decoder_1_out14), .out15(decoder_1_out15), .sel(IMM));  // open: out12
  or or_1 (or_1_out, decoder_1_out13, or_2_out);
  or or_2 (or_2_out, decoder_1_out14, decoder_1_out15);
  or or_3 (I[0], decoder_1_out0, or_1_out);
  or or_4 (I[1], decoder_1_out1, or_1_out);
  or or_5 (I[2], decoder_1_out2, or_1_out);
  or or_6 (I[3], decoder_1_out3, or_1_out);
  or or_7 (I[4], decoder_1_out4, or_2_out);
  or or_8 (I[5], decoder_1_out5, or_2_out);
  or or_9 (I[6], decoder_1_out6, or_2_out);
  or or_10 (I[7], decoder_1_out7, or_2_out);
  or or_11 (I[8], decoder_1_out8, decoder_1_out15);
  or or_12 (I[9], decoder_1_out9, decoder_1_out15);
  or or_13 (I[10], decoder_1_out10, decoder_1_out15);
  or or_14 (I[11], decoder_1_out11, decoder_1_out15);
  Pull_Resistor pull_resistor_1 (.node(I));
endmodule

module Inverter (
  input  [3:0] in_1,
  input  in_2,
  output [3:0] out_3
);

  wire not_1_out;

  assign out_3 = not_1_out ? in_1 : 4'bz;  // Controlled_Buffer controlled_buffer_1
  not not_1 (not_1_out, in_2);
  assign out_3 = in_2 ? ~in_1 : 4'bz;  // Controlled_Inverter controlled_inverter_1
endmodule

module Overflow (
  input  L,
  input  R,
  input  Z,
  output V
);

  wire xnor_1_out, xor_1_out;

  xnor xnor_1 (xnor_1_out, L, R);
  xor xor_1 (xor_1_out, L, Z);
  and and_1 (V, xnor_1_out, xor_1_out);
endmodule

module ALU (
  input  [3:0] L,
  input  [3:0] R,
  input  C,
  input  [2:0] OP,
  output [3:0] Z,
  output C_2,
  output Z_2,
  output N,
  output V
);

  wire adder_1_cout, xor_1_out;
  wire [3:0] adder_1_out, and_1_out, inverter_1_out_3, or_1_out, xor_2_out;

  Inverter inverter_1 (.in_1(R), .in_2(OP[2]), .out_3(inverter_1_out_3));
  xor xor_1 (xor_1_out, C, OP[2]);
  assign and_1_out = L & inverter_1_out_3;  // AND_Gate and_1, 4 bits wide
  assign or_1_out = L | inverter_1_out_3;  // OR_Gate or_1, 4 bits wide
  assign xor_2_out = L ^ inverter_1_out_3;  // XOR_Gate xor_2, 4 bits wide
  Adder #(.width(4)) adder_1 (.a(L), .b(inverter_1_out_3), .out(adder_1_out), .cin(xor_1_out), .cout(adder_1_cout));
  Multiplexer #(.select(3), .width(4), .enable("false")) multiplexer_1 (
    .in0(adder_1_out), .in1(and_1_out), .in2(or_1_out), .in3(xor_2_out), .in4(adder_1_out), .in5(and_1_out),
    .in6(or_1_out), .in7({L[2:0], C}), .out({N, Z[2:0]}), .sel(OP));
  Multiplexer #(.select(3), .enable("false")) multiplexer_2 (
    .in0(adder_1_cout), .in1(L[3]), .in2(L[3]), .in3(L[3]), .in4(adder_1_cout), .in5(L[3]), .in6(L[3]),
    .in7(L[3]), .out(C_2), .sel(OP));
  nand nand_1 (Z_2, Z[0], Z[1], Z[2], N);
  Overflow overflow_1 (.L(L[3]), .R(inverter_1_out_3[3]), .Z(N), .V(V));

  assign Z[3] = N;
endmodule

module Full_ALU (
  input  C,
  input  [15:0] L,
  input  [15:0] R,
  input  [2:0] OP,
  output [15:0] Z,
  output C_2,
  output Z_2,
  output N,
  output V
);

  wire alu_1_c_2, alu_1_z_2, alu_2_c_2, alu_2_z_2, alu_3_c_2, alu_3_z_2, alu_4_z_2;

  ALU alu_1 (.L(L[3:0]), .R(R[3:0]), .C(C), .OP(OP), .Z(Z[3:0]), .C_2(alu_1_c_2), .Z_2(alu_1_z_2));  // open: N, V
  ALU alu_2 (
    .L(L[7:4]), .R(R[7:4]), .C(alu_1_c_2), .OP(OP), .Z(Z[7:4]), .C_2(alu_2_c_2), .Z_2(alu_2_z_2));  // open: N, V
  ALU alu_3 (
    .L(L[11:8]), .R(R[11:8]), .C(alu_2_c_2), .OP(OP), .Z(Z[11:8]), .C_2(alu_3_c_2), .Z_2(alu_3_z_2));  // open: N, V
  ALU alu_4 (
    .L(L[15:12]), .R(R[15:12]), .C(alu_3_c_2), .OP(OP), .Z(Z[15:12]), .C_2(C_2), .Z_2(alu_4_z_2), .N(N), .V(V));
  and and_1 (Z_2, alu_1_z_2, alu_2_z_2, alu_3_z_2, alu_4_z_2);
endmodule

module Conditions (
  input  C,
  input  Z,
  input  N,
  input  V,
  input  [2:0] CONDITION,
  output TRUE
);

  wire and_1_out, not_1_out, or_1_out, pull_resistor_1_node, xor_1_out;

  not not_1 (not_1_out, Z);
  Pull_Resistor pull_resistor_1 (.node(pull_resistor_1_node));
  and and_1 (and_1_out, C, not_1_out);
  xor xor_1 (xor_1_out, N, V);
  or or_1 (or_1_out, xor_1_out, Z);
  Multiplexer #(.select(3), .enable("false")) multiplexer_1 (
    .in0(pull_resistor_1_node), .in1(and_1_out), .in2(xor_1_out), .in3(or_1_out), .in4(C), .in5(Z), .in6(N),
    .in7(V), .out(TRUE), .sel(CONDITION));
endmodule

module NextState (
  input  C,
  input  Z,
  input  N,
  input  V,
  input  [2:0] COND,
  input  [15:0] MDR,
  input  [11:0] NEXT_STATE,
  input  nFAULT,
  output [11:0] out_9
);

  wire conditions_1_true, or_1_out;
  wire [0:0] xor_1_out;
  wire [11:0] multiplexer_1_out;

  Conditions conditions_1 (.C(C), .Z(Z), .N(N), .V(V), .CONDITION(COND), .TRUE(conditions_1_true));
  xor xor_1 (xor_1_out[0], conditions_1_true, NEXT_STATE[0]);
  or or_1 (or_1_out, NEXT_STATE[0], NEXT_STATE[1], NEXT_STATE[2], NEXT_STATE[3], NEXT_STATE[4], NEXT_STATE[5], NEXT_STATE[6], NEXT_STATE[7], NEXT_STATE[8], NEXT_STATE[9], NEXT_STATE[10], NEXT_STATE[11]);
  Multiplexer #(.width(12), .enable("false")) multiplexer_1 (
    .in0({4'b0000, MDR[7:0]}), .in1({NEXT_STATE[11:1], xor_1_out[0]}), .out(multiplexer_1_out), .sel(or_1_out));
  Pull_Resistor pull_resistor_1 (.node(out_9));
  assign out_9 = nFAULT ? multiplexer_1_out : 12'bz;  // Controlled_Buffer controlled_buffer_1
endmodule

module StateMachine (
  input  C,
  input  Z,
  input  N,
  input  V,
  input  [15:0] MDR,
  input  nFAULT,
  input  CLK,
  input  RST,
  output PRIVILEDGED,
  output LATCH_ADDR,
  output LATCH_FLAGS,
  output [2:0] ALU_OP,
  output [1:0] ALU_CARRY,
  output [1:0] ADDR_REG,
  output BUS_DIR,
  output BUS_BYTE,
  output MDR_SOURCE,
  output TLB_DISABLE,
  output [1:0] TLB_WRITE,
  output [3:0] L_BUS,
  output [1:0] R_BUS,
  output [2:0] Z_REG,
  output [2:0] Z_ADDR,
  output [3:0] IMMEDIATE,
  output FLAG_SOURCE
);

  wire [2:0] microcode_1_condition;
  wire [11:0] microcode_1_next_state, nextstate_1_out_9, register_1_q;

  NextState nextstate_1 (
    .C(C), .Z(Z), .N(N), .V(V), .COND(microcode_1_condition), .MDR(MDR), .NEXT_STATE(microcode_1_next_state),
    .nFAULT(nFAULT), .out_9(nextstate_1_out_9));
  Register #(.width(12)) register_1 (.D(nextstate_1_out_9), .Q(register_1_q), .clk(CLK), .clr(RST));  // open: en
  MicroCode microcode_1 (
    .STATE(register_1_q), .PRIVILEDGED(PRIVILEDGED), .LATCH_ADDR(LATCH_ADDR), .LATCH_FLAGS(LATCH_FLAGS),
    .ALU_OP(ALU_OP), .ALU_CARRY(ALU_CARRY), .ADDR_REG(ADDR_REG), .BUS_DIR(BUS_DIR), .BUS_BYTE(BUS_BYTE),
    .MDR_SOURCE(MDR_SOURCE), .TLB_DISABLE(TLB_DISABLE), .TLB_WRITE(TLB_WRITE), .L_BUS(L_BUS), .R_BUS(R_BUS),
    .Z_REG(Z_REG), .Z_ADDR(Z_ADDR), .IMMEDIATE(IMMEDIATE), .FLAG_SOURCE(FLAG_SOURCE),
    .CONDITION(microcode_1_condition), .NEXT_STATE(microcode_1_next_state));
endmodule

module TLB_Index (
  input  SELECT,
  input  CLK,
  input  RESET,
  input  WRITE_BANK,
  input  WRITE_FLAG,
  input  [15:0] ZBUS,
  input  [11:0] UPPER_ADDR,
  input  [3:0] PID,
  output CLK_2,
  output RESET_2,
  output WRITE_BANK_2,
  output WRITE_FLAG_2,
  output [15:0] ZBUS_2,
  output [11:0] UPPER_ADDR_2,
  output [3:0] PID_2,
  output READ,
  output WRITE,
  output ACTIVE,
  output [11:0] BANK
);

  wire and_1_out, and_2_out, and_3_out, comparator_1_eq;
  wire [3:3] controlled_buffer_1_out;
  wire [15:0] register_1_q, register_2_q;

  and and_1 (and_1_out, WRITE_BANK, SELECT);
  and and_2 (and_2_out, WRITE_FLAG, SELECT);
  Register #(.width(16)) register_1 (.D(ZBUS), .en(and_1_out), .Q(register_1_q), .clk(CLK), .clr(RESET));
  Register #(.width(16)) register_2 (.D(ZBUS), .en(and_2_out), .Q(register_2_q), .clk(CLK), .clr(RESET));
  Comparator #(.width(16)) comparator_1 (
    .a(register_2_q), .b({UPPER_ADDR, PID}), .eq(comparator_1_eq));  // open: gt, lt
  assign {BANK, controlled_buffer_1_out[3], ACTIVE, WRITE, READ} = and_3_out ? register_1_q : 16'bz;  // Controlled_Buffer controlled_buffer_1
  and and_3 (and_3_out, register_1_q[2], comparator_1_eq);

  assign CLK_2 = CLK;
  assign PID_2 = PID;
  assign RESET_2 = RESET;
  assign UPPER_ADDR_2 = UPPER_ADDR;
  assign WRITE_BANK_2 = WRITE_BANK;
  assign WRITE_FLAG_2 = WRITE_FLAG;
  assign ZBUS_2 = ZBUS;
endmodule

module TLB_Matrix (
  input  [3:0] INDEX,
  input  CLK,
  input  RESET,
  input  WRITE_BANK,
  input  WRITE_FLAG,
  input  [15:0] ZBUS,
  input  [11:0] UPPER_ADDR,
  input  [3:0] PID,
  output READ,
  output WRITE,
  output ACTIVE,
  output [11:0] BANK
);

  wire decoder_1_out0, decoder_1_out1, decoder_1_out2, decoder_1_out3, decoder_1_out4, decoder_1_out5,
       decoder_1_out6, decoder_1_out7, decoder_1_out8, decoder_1_out9, decoder_1_out10, decoder_1_out11,
       decoder_1_out12, decoder_1_out13, decoder_1_out14, decoder_1_out15, tlb_index_1_clk_2,
       tlb_index_1_reset_2, tlb_index_1_write_bank_2, tlb_index_1_write_flag_2, tlb_index_2_clk_2,
       tlb_index_2_reset_2, tlb_index_2_write_bank_2, tlb_index_2_write_flag_2, tlb_index_3_active,
       tlb_index_3_clk_2, tlb_index_3_read, tlb_index_3_reset_2, tlb_index_3_write, tlb_index_3_write_bank_2,
       tlb_index_3_write_flag_2, tlb_index_4_clk_2, tlb_index_4_reset_2, tlb_index_4_write_bank_2,
       tlb_index_4_write_flag_2, tlb_index_5_active, tlb_index_5_clk_2, tlb_index_5_read,
       tlb_index_5_reset_2, tlb_index_5_write, tlb_index_5_write_bank_2, tlb_index_5_write_flag_2,
       tlb_index_6_clk_2, tlb_index_6_reset_2, tlb_index_6_write_bank_2, tlb_index_6_write_flag_2,
       tlb_index_7_active, tlb_index_7_clk_2, tlb_index_7_read, tlb_index_7_reset_2, tlb_index_7_write,
       tlb_index_7_write_bank_2, tlb_index_7_write_flag_2, tlb_index_8_clk_2, tlb_index_8_reset_2,
       tlb_index_8_write_bank_2, tlb_index_8_write_flag_2, tlb_index_9_active, tlb_index_9_clk_2,
       tlb_index_9_read, tlb_index_9_reset_2, tlb_index_9_write, tlb_index_9_write_bank_2,
       tlb_index_9_write_flag_2, tlb_index_10_clk_2, tlb_index_10_reset_2, tlb_index_10_write_bank_2,
       tlb_index_10_write_flag_2, tlb_index_11_active, tlb_index_11_clk_2, tlb_index_11_read,
       tlb_index_11_reset_2, tlb_index_11_write, tlb_index_11_write_bank_2, tlb_index_11_write_flag_2,
       tlb_index_12_clk_2, tlb_index_12_reset_2, tlb_index_12_write_bank_2, tlb_index_12_write_flag_2,
       tlb_index_13_active, tlb_index_13_clk_2, tlb_index_13_read, tlb_index_13_reset_2, tlb_index_13_write,
       tlb_index_13_write_bank_2, tlb_index_13_write_flag_2, tlb_index_14_clk_2, tlb_index_14_reset_2,
       tlb_index_14_write_bank_2, tlb_index_14_write_flag_2;
  wire [3:0] tlb_index_1_pid_2, tlb_index_2_pid_2, tlb_index_3_pid_2, tlb_index_4_pid_2, tlb_index_5_pid_2,
       tlb_index_6_pid_2, tlb_index_7_pid_2, tlb_index_8_pid_2, tlb_index_9_pid_2, tlb_index_10_pid_2,
       tlb_index_11_pid_2, tlb_index_12_pid_2, tlb_index_13_pid_2, tlb_index_14_pid_2;
  wire [11:0] tlb_index_1_upper_addr_2, tlb_index_2_upper_addr_2, tlb_index_3_bank, tlb_index_3_upper_addr_2,
       tlb_index_4_upper_addr_2, tlb_index_5_bank, tlb_index_5_upper_addr_2, tlb_index_6_upper_addr_2,
       tlb_index_7_bank, tlb_index_7_upper_addr_2, tlb_index_8_upper_addr_2, tlb_index_9_bank,
       tlb_index_9_upper_addr_2, tlb_index_10_upper_addr_2, tlb_index_11_bank, tlb_index_11_upper_addr_2,
       tlb_index_12_upper_addr_2, tlb_index_13_bank, tlb_index_13_upper_addr_2, tlb_index_14_upper_addr_2;
  wire [15:0] tlb_index_1_zbus_2, tlb_index_2_zbus_2, tlb_index_3_zbus_2, tlb_index_4_zbus_2,
       tlb_index_5_zbus_2, tlb_index_6_zbus_2, tlb_index_7_zbus_2, tlb_index_8_zbus_2, tlb_index_9_zbus_2,
       tlb_index_10_zbus_2, tlb_index_11_zbus_2, tlb_index_12_zbus_2, tlb_index_13_zbus_2,
       tlb_index_14_zbus_2;

  Decoder #(.select(4), .enable("false")) decoder_1 (
    .out0(decoder_1_out0), .out1(decoder_1_out1), .out2(decoder_1_out2), .out3(decoder_1_out3),
    .out4(decoder_1_out4), .out5(decoder_1_out5), .out6(decoder_1_out6), .out7(decoder_1_out7),
    .out8(decoder_1_out8), .out9(decoder_1_out9), .out10(decoder_1_out10), .out11(decoder_1_out11),
    .out12(decoder_1_out12), .out13(decoder_1_out13), .out14(decoder_1_out14), .out15(decoder_1_out15),
    .sel(INDEX));
  TLB_Index tlb_index_1 (
    .SELECT(decoder_1_out7), .CLK(CLK), .RESET(RESET), .WRITE_BANK(WRITE_BANK), .WRITE_FLAG(WRITE_FLAG),
    .ZBUS(ZBUS), .UPPER_ADDR(UPPER_ADDR), .PID(PID), .CLK_2(tlb_index_1_clk_2),
    .RESET_2(tlb_index_1_reset_2), .WRITE_BANK_2(tlb_index_1_write_bank_2),
    .WRITE_FLAG_2(tlb_index_1_write_flag_2), .ZBUS_2(tlb_index_1_zbus_2),
    .UPPER_ADDR_2(tlb_index_1_upper_addr_2), .PID_2(tlb_index_1_pid_2), .READ(READ), .WRITE(WRITE),
    .ACTIVE(ACTIVE), .BANK(BANK));
  TLB_Index tlb_index_2 (
    .SELECT(decoder_1_out8), .CLK(CLK), .RESET(RESET), .WRITE_BANK(WRITE_BANK), .WRITE_FLAG(WRITE_FLAG),
    .ZBUS(ZBUS), .UPPER_ADDR(UPPER_ADDR), .PID(PID), .CLK_2(tlb_index_2_clk_2),
    .RESET_2(tlb_index_2_reset_2), .WRITE_BANK_2(tlb_index_2_write_bank_2),
    .WRITE_FLAG_2(tlb_index_2_write_flag_2), .ZBUS_2(tlb_index_2_zbus_2),
    .UPPER_ADDR_2(tlb_index_2_upper_addr_2), .PID_2(tlb_index_2_pid_2), .READ(READ), .WRITE(WRITE),
    .ACTIVE(ACTIVE), .BANK(BANK));
  TLB_Index tlb_index_3 (
    .SELECT(decoder_1_out6), .CLK(tlb_index_1_clk_2), .RESET(tlb_index_1_reset_2),
    .WRITE_BANK(tlb_index_1_write_bank_2), .WRITE_FLAG(tlb_index_1_write_flag_2), .ZBUS(tlb_index_1_zbus_2),
    .UPPER_ADDR(tlb_index_1_upper_addr_2), .PID(tlb_index_1_pid_2), .CLK_2(tlb_index_3_clk_2),
    .RESET_2(tlb_index_3_reset_2), .WRITE_BANK_2(tlb_index_3_write_bank_2),
    .WRITE_FLAG_2(tlb_index_3_write_flag_2), .ZBUS_2(tlb_index_3_zbus_2),
    .UPPER_ADDR_2(tlb_index_3_upper_addr_2), .PID_2(tlb_index_3_pid_2), .READ(tlb_index_3_read),
    .WRITE(tlb_index_3_write), .ACTIVE(tlb_index_3_active), .BANK(tlb_index_3_bank));
  TLB_Index tlb_index_4 (
    .SELECT(decoder_1_out9), .CLK(tlb_index_2_clk_2), .RESET(tlb_index_2_reset_2),
    .WRITE_BANK(tlb_index_2_write_bank_2), .WRITE_FLAG(tlb_index_2_write_flag_2), .ZBUS(tlb_index_2_zbus_2),
    .UPPER_ADDR(tlb_index_2_upper_addr_2), .PID(tlb_index_2_pid_2), .CLK_2(tlb_index_4_clk_2),
    .RESET_2(tlb_index_4_reset_2), .WRITE_BANK_2(tlb_index_4_write_bank_2),
    .WRITE_FLAG_2(tlb_index_4_write_flag_2), .ZBUS_2(tlb_index_4_zbus_2),
    .UPPER_ADDR_2(tlb_index_4_upper_addr_2), .PID_2(tlb_index_4_pid_2), .READ(tlb_index_3_read),
    .WRITE(tlb_index_3_write), .ACTIVE(tlb_index_3_active), .BANK(tlb_index_3_bank));
  TLB_Index tlb_index_5 (
    .SELECT(decoder_1_out5), .CLK(tlb_index_3_clk_2), .RESET(tlb_index_3_reset_2),
    .WRITE_BANK(tlb_index_3_write_bank_2), .WRITE_FLAG(tlb_index_3_write_flag_2), .ZBUS(tlb_index_3_zbus_2),
    .UPPER_ADDR(tlb_index_3_upper_addr_2), .PID(tlb_index_3_pid_2), .CLK_2(tlb_index_5_clk_2),
    .RESET_2(tlb_index_5_reset_2), .WRITE_BANK_2(tlb_index_5_write_bank_2),
    .WRITE_FLAG_2(tlb_index_5_write_flag_2), .ZBUS_2(tlb_index_5_zbus_2),
    .UPPER_ADDR_2(tlb_index_5_upper_addr_2), .PID_2(tlb_index_5_pid_2), .READ(tlb_index_5_read),
    .WRITE(tlb_index_5_write), .ACTIVE(tlb_index_5_active), .BANK(tlb_index_5_bank));
  TLB_Index tlb_index_6 (
    .SELECT(decoder_1_out10), .CLK(tlb_index_4_clk_2), .RESET(tlb_index_4_reset_2),
    .WRITE_BANK(tlb_index_4_write_bank_2), .WRITE_FLAG(tlb_index_4_write_flag_2), .ZBUS(tlb_index_4_zbus_2),
    .UPPER_ADDR(tlb_index_4_upper_addr_2), .PID(tlb_index_4_pid_2), .CLK_2(tlb_index_6_clk_2),
    .RESET_2(tlb_index_6_reset_2), .WRITE_BANK_2(tlb_index_6_write_bank_2),
    .WRITE_FLAG_2(tlb_index_6_write_flag_2), .ZBUS_2(tlb_index_6_zbus_2),
    .UPPER_ADDR_2(tlb_index_6_upper_addr_2), .PID_2(tlb_index_6_pid_2), .READ(tlb_index_5_read),
    .WRITE(tlb_index_5_write), .ACTIVE(tlb_index_5_active), .BANK(tlb_index_5_bank));
  TLB_Index tlb_index_7 (
    .SELECT(decoder_1_out4), .CLK(tlb_index_5_clk_2), .RESET(tlb_index_5_reset_2),
    .WRITE_BANK(tlb_index_5_write_bank_2), .WRITE_FLAG(tlb_index_5_write_flag_2), .ZBUS(tlb_index_5_zbus_2),
    .UPPER_ADDR(tlb_index_5_upper_addr_2), .PID(tlb_index_5_pid_2), .CLK_2(tlb_index_7_clk_2),
    .RESET_2(tlb_index_7_reset_2), .WRITE_BANK_2(tlb_index_7_write_bank_2),
    .WRITE_FLAG_2(tlb_index_7_write_flag_2), .ZBUS_2(tlb_index_7_zbus_2),
    .UPPER_ADDR_2(tlb_index_7_upper_addr_2), .PID_2(tlb_index_7_pid_2), .READ(tlb_index_7_read),
    .WRITE(tlb_index_7_write), .ACTIVE(tlb_index_7_active), .BANK(tlb_index_7_bank));
  TLB_Index tlb_index_8 (
    .SELECT(decoder_1_out11), .CLK(tlb_index_6_clk_2), .RESET(tlb_index_6_reset_2),
    .WRITE_BANK(tlb_index_6_write_bank_2), .WRITE_FLAG(tlb_index_6_write_flag_2), .ZBUS(tlb_index_6_zbus_2),
    .UPPER_ADDR(tlb_index_6_upper_addr_2), .PID(tlb_index_6_pid_2), .CLK_2(tlb_index_8_clk_2),
    .RESET_2(tlb_index_8_reset_2), .WRITE_BANK_2(tlb_index_8_write_bank_2),
    .WRITE_FLAG_2(tlb_index_8_write_flag_2), .ZBUS_2(tlb_index_8_zbus_2),
    .UPPER_ADDR_2(tlb_index_8_upper_addr_2), .PID_2(tlb_index_8_pid_2), .READ(tlb_index_7_read),
    .WRITE(tlb_index_7_write), .ACTIVE(tlb_index_7_active), .BANK(tlb_index_7_bank));
  TLB_Index tlb_index_9 (
    .SELECT(decoder_1_out3), .CLK(tlb_index_7_clk_2), .RESET(tlb_index_7_reset_2),
    .WRITE_BANK(tlb_index_7_write_bank_2), .WRITE_FLAG(tlb_index_7_write_flag_2), .ZBUS(tlb_index_7_zbus_2),
    .UPPER_ADDR(tlb_index_7_upper_addr_2), .PID(tlb_index_7_pid_2), .CLK_2(tlb_index_9_clk_2),
    .RESET_2(tlb_index_9_reset_2), .WRITE_BANK_2(tlb_index_9_write_bank_2),
    .WRITE_FLAG_2(tlb_index_9_write_flag_2), .ZBUS_2(tlb_index_9_zbus_2),
    .UPPER_ADDR_2(tlb_index_9_upper_addr_2), .PID_2(tlb_index_9_pid_2), .READ(tlb_index_9_read),
    .WRITE(tlb_index_9_write), .ACTIVE(tlb_index_9_active), .BANK(tlb_index_9_bank));
  TLB_Index tlb_index_10 (
    .SELECT(decoder_1_out12), .CLK(tlb_index_8_clk_2), .RESET(tlb_index_8_reset_2),
    .WRITE_BANK(tlb_index_8_write_bank_2), .WRITE_FLAG(tlb_index_8_write_flag_2), .ZBUS(tlb_index_8_zbus_2),
    .UPPER_ADDR(tlb_index_8_upper_addr_2), .PID(tlb_index_8_pid_2), .CLK_2(tlb_index_10_clk_2),
    .RESET_2(tlb_index_10_reset_2), .WRITE_BANK_2(tlb_index_10_write_bank_2),
    .WRITE_FLAG_2(tlb_index_10_write_flag_2), .ZBUS_2(tlb_index_10_zbus_2),
    .UPPER_ADDR_2(tlb_index_10_upper_addr_2), .PID_2(tlb_index_10_pid_2), .READ(tlb_index_9_read),
    .WRITE(tlb_index_9_write), .ACTIVE(tlb_index_9_active), .BANK(tlb_index_9_bank));
  TLB_Index tlb_index_11 (
    .SELECT(decoder_1_out2), .CLK(tlb_index_9_clk_2), .RESET(tlb_index_9_reset_2),
    .WRITE_BANK(tlb_index_9_write_bank_2), .WRITE_FLAG(tlb_index_9_write_flag_2), .ZBUS(tlb_index_9_zbus_2),
    .UPPER_ADDR(tlb_index_9_upper_addr_2), .PID(tlb_index_9_pid_2), .CLK_2(tlb_index_11_clk_2),
    .RESET_2(tlb_index_11_reset_2), .WRITE_BANK_2(tlb_index_11_write_bank_2),
    .WRITE_FLAG_2(tlb_index_11_write_flag_2), .ZBUS_2(tlb_index_11_zbus_2),
    .UPPER_ADDR_2(tlb_index_11_upper_addr_2), .PID_2(tlb_index_11_pid_2), .READ(tlb_index_11_read),
    .WRITE(tlb_index_11_write), .ACTIVE(tlb_index_11_active), .BANK(tlb_index_11_bank));
  TLB_Index tlb_index_12 (
    .SELECT(decoder_1_out13), .CLK(tlb_index_10_clk_2), .RESET(tlb_index_10_reset_2),
    .WRITE_BANK(tlb_index_10_write_bank_2), .WRITE_FLAG(tlb_index_10_write_flag_2),
    .ZBUS(tlb_index_10_zbus_2), .UPPER_ADDR(tlb_index_10_upper_addr_2), .PID(tlb_index_10_pid_2),
    .CLK_2(tlb_index_12_clk_2), .RESET_2(tlb_index_12_reset_2), .WRITE_BANK_2(tlb_index_12_write_bank_2),
    .WRITE_FLAG_2(tlb_index_12_write_flag_2), .ZBUS_2(tlb_index_12_zbus_2),
    .UPPER_ADDR_2(tlb_index_12_upper_addr_2), .PID_2(tlb_index_12_pid_2), .READ(tlb_index_11_read),
    .WRITE(tlb_index_11_write), .ACTIVE(tlb_index_11_active), .BANK(tlb_index_11_bank));
  TLB_Index tlb_index_13 (
    .SELECT(decoder_1_out1), .CLK(tlb_index_11_clk_2), .RESET(tlb_index_11_reset_2),
    .WRITE_BANK(tlb_index_11_write_bank_2), .WRITE_FLAG(tlb_index_11_write_flag_2),
    .ZBUS(tlb_index_11_zbus_2), .UPPER_ADDR(tlb_index_11_upper_addr_2), .PID(tlb_index_11_pid_2),
    .CLK_2(tlb_index_13_clk_2), .RESET_2(tlb_index_13_reset_2), .WRITE_BANK_2(tlb_index_13_write_bank_2),
    .WRITE_FLAG_2(tlb_index_13_write_flag_2), .ZBUS_2(tlb_index_13_zbus_2),
    .UPPER_ADDR_2(tlb_index_13_upper_addr_2), .PID_2(tlb_index_13_pid_2), .READ(tlb_index_13_read),
    .WRITE(tlb_index_13_write), .ACTIVE(tlb_index_13_active), .BANK(tlb_index_13_bank));
  TLB_Index tlb_index_14 (
    .SELECT(decoder_1_out14), .CLK(tlb_index_12_clk_2), .RESET(tlb_index_12_reset_2),
    .WRITE_BANK(tlb_index_12_write_bank_2), .WRITE_FLAG(tlb_index_12_write_flag_2),
    .ZBUS(tlb_index_12_zbus_2), .UPPER_ADDR(tlb_index_12_upper_addr_2), .PID(tlb_index_12_pid_2),
    .CLK_2(tlb_index_14_clk_2), .RESET_2(tlb_index_14_reset_2), .WRITE_BANK_2(tlb_index_14_write_bank_2),
    .WRITE_FLAG_2(tlb_index_14_write_flag_2), .ZBUS_2(tlb_index_14_zbus_2),
    .UPPER_ADDR_2(tlb_index_14_upper_addr_2), .PID_2(tlb_index_14_pid_2), .READ(tlb_index_13_read),
    .WRITE(tlb_index_13_write), .ACTIVE(tlb_index_13_active), .BANK(tlb_index_13_bank));
  TLB_Index tlb_index_15 (
    .SELECT(decoder_1_out0), .CLK(tlb_index_13_clk_2), .RESET(tlb_index_13_reset_2),
    .WRITE_BANK(tlb_index_13_write_bank_2), .WRITE_FLAG(tlb_index_13_write_flag_2),
    .ZBUS(tlb_index_13_zbus_2), .UPPER_ADDR(tlb_index_13_upper_addr_2), .PID(tlb_index_13_pid_2),
    .READ(READ), .WRITE(WRITE), .ACTIVE(ACTIVE), .BANK(BANK));  // open: CLK_2, RESET_2, WRITE_BANK_2, WRITE_FLAG_2, ZBUS_2, UPPER_ADDR_2, PID_2
  TLB_Index tlb_index_16 (
    .SELECT(decoder_1_out15), .CLK(tlb_index_14_clk_2), .RESET(tlb_index_14_reset_2),
    .WRITE_BANK(tlb_index_14_write_bank_2), .WRITE_FLAG(tlb_index_14_write_flag_2),
    .ZBUS(tlb_index_14_zbus_2), .UPPER_ADDR(tlb_index_14_upper_addr_2), .PID(tlb_index_14_pid_2),
    .READ(READ), .WRITE(WRITE), .ACTIVE(ACTIVE), .BANK(BANK));  // open: CLK_2, RESET_2, WRITE_BANK_2, WRITE_FLAG_2, ZBUS_2, UPPER_ADDR_2, PID_2
endmodule

module TLB_Main (
  input  [1:0] TLB_WRITE,
  input  CLK,
  input  RESET,
  input  [15:0] ZBUS,
  input  [23:0] ADDR,
  input  [3:0] PID,
  input  TLB_DISABLE,
  output READ,
  output WRITE,
  output ACTIVE,
  output [23:0] ADDR_2
);

  wire decoder_1_out1, decoder_1_out2, decoder_1_out3, not_1_out, pull_resistor_1_node, pull_resistor_2_node,
       tlb_matrix_1_active;
  wire [3:0] register_1_q;
  wire [11:0] tlb_matrix_1_bank;

  Decoder #(.select(2), .enable("false")) decoder_1 (
    .out1(decoder_1_out1), .out2(decoder_1_out2), .out3(decoder_1_out3), .sel(TLB_WRITE));  // open: out0
  Register #(.width(4)) register_1 (.D(ZBUS[3:0]), .en(decoder_1_out1), .Q(register_1_q), .clk(CLK), .clr(RESET));
  Pull_Resistor pull_resistor_1 (.node(pull_resistor_1_node));
  Pull_Resistor pull_resistor_2 (.node(pull_resistor_2_node));
  TLB_Matrix tlb_matrix_1 (
    .INDEX(register_1_q), .CLK(CLK), .RESET(RESET), .WRITE_BANK(decoder_1_out3), .WRITE_FLAG(decoder_1_out2),
    .ZBUS(ZBUS), .UPPER_ADDR(ADDR[23:12]), .PID(PID), .READ(pull_resistor_1_node),
    .WRITE(pull_resistor_2_node), .ACTIVE(tlb_matrix_1_active), .BANK(tlb_matrix_1_bank));
  not not_1 (not_1_out, TLB_DISABLE);
  Pull_Resistor pull_resistor_3 (.node(ADDR_2[23:12]));
  Pull_Resistor pull_resistor_4 (.node(tlb_matrix_1_active));
  assign ADDR_2[23:12] = not_1_out ? tlb_matrix_1_bank : 12'bz;  // Controlled_Buffer controlled_buffer_1
  assign ADDR_2[23:12] = TLB_DISABLE ? ADDR[23:12] : 12'bz;  // Controlled_Buffer controlled_buffer_2
  or or_1 (READ, pull_resistor_1_node, TLB_DISABLE);
  or or_2 (WRITE, pull_resistor_2_node, TLB_DISABLE);
  or or_3 (ACTIVE, tlb_matrix_1_active, TLB_DISABLE);

  assign ADDR_2[11:0] = ADDR[11:0];
endmodule
