// Logisim project EdgeComputer.circ as structural Verilog
module SN74172_Register (
  input  [15:0] D0,
  input  [15:0] D1,
  input  WR0,
  input  WR1,
  input  CLK,
  output [15:0] Q
);

  wire or_1_out;
  wire [15:0] and_1_out, pull_resistor_1_node, pull_resistor_2_node;

  Pull_Resistor #(.pull(1)) pull_resistor_1 (.node(pull_resistor_1_node));
  Pull_Resistor #(.pull(1)) pull_resistor_2 (.node(pull_resistor_2_node));
  assign pull_resistor_1_node = WR0 ? D0 : 16'bz;  // Controlled_Buffer controlled_buffer_1
  assign pull_resistor_2_node = WR1 ? D1 : 16'bz;  // Controlled_Buffer controlled_buffer_2
  assign and_1_out = pull_resistor_1_node & pull_resistor_2_node;  // AND_Gate and_1, 16 bits wide
  or or_1 (or_1_out, WR0, WR1);
  Register #(.width(16)) register_1 (.D(and_1_out), .en(or_1_out), .Q(Q), .clk(CLK));  // open: clr
endmodule

module DualPort_Reg_File (
  input  CLK,
  input  [15:0] D0,
  input  [15:0] D1,
  input  [2:0] W0,
  input  [2:0] R0,
  input  [2:0] WR1,
  input  nWE0,
  input  nWE1,
  input  nRE0,
  input  nRE1,
  output [15:0] Q0,
  output [15:0] Q1
);

  wire decoder_1_out0, decoder_1_out1, decoder_1_out2, decoder_1_out3, decoder_1_out4, decoder_1_out5,
       decoder_1_out6, decoder_1_out7, decoder_2_out0, decoder_2_out1, decoder_2_out2, decoder_2_out3,
       decoder_2_out4, decoder_2_out5, decoder_2_out6, decoder_2_out7, not_1_out, not_2_out, not_3_out,
       not_4_out;
  wire [15:0] sn74172_register_1_q, sn74172_register_2_q, sn74172_register_3_q, sn74172_register_4_q,
       sn74172_register_5_q, sn74172_register_6_q, sn74172_register_7_q, sn74172_register_8_q;

  not not_1 (not_1_out, nWE0);
  not not_2 (not_2_out, nWE1);
  not not_3 (not_3_out, nRE0);
  not not_4 (not_4_out, nRE1);
  Decoder #(.select(3), .disabled(0)) decoder_1 (
    .out0(decoder_1_out0), .out1(decoder_1_out1), .out2(decoder_1_out2), .out3(decoder_1_out3),
    .out4(decoder_1_out4), .out5(decoder_1_out5), .out6(decoder_1_out6), .out7(decoder_1_out7), .sel(W0),
    .en(not_1_out));
  Decoder #(.select(3), .disabled(0)) decoder_2 (
    .out0(decoder_2_out0), .out1(decoder_2_out1), .out2(decoder_2_out2), .out3(decoder_2_out3),
    .out4(decoder_2_out4), .out5(decoder_2_out5), .out6(decoder_2_out6), .out7(decoder_2_out7), .sel(WR1),
    .en(not_2_out));
  SN74172_Register sn74172_register_1 (
    .D0(D0), .D1(D1), .WR0(decoder_1_out0), .WR1(decoder_2_out0), .CLK(CLK), .Q(sn74172_register_1_q));
  SN74172_Register sn74172_register_2 (
    .D0(D0), .D1(D1), .WR0(decoder_1_out1), .WR1(decoder_2_out1), .CLK(CLK), .Q(sn74172_register_2_q));
  SN74172_Register sn74172_register_3 (
    .D0(D0), .D1(D1), .WR0(decoder_1_out2), .WR1(decoder_2_out2), .CLK(CLK), .Q(sn74172_register_3_q));
  SN74172_Register sn74172_register_4 (
    .D0(D0), .D1(D1), .WR0(decoder_1_out3), .WR1(decoder_2_out3), .CLK(CLK), .Q(sn74172_register_4_q));
  SN74172_Register sn74172_register_5 (
    .D0(D0), .D1(D1), .WR0(decoder_1_out4), .WR1(decoder_2_out4), .CLK(CLK), .Q(sn74172_register_5_q));
  SN74172_Register sn74172_register_6 (
    .D0(D0), .D1(D1), .WR0(decoder_1_out5), .WR1(decoder_2_out5), .CLK(CLK), .Q(sn74172_register_6_q));
  SN74172_Register sn74172_register_7 (
    .D0(D0), .D1(D1), .WR0(decoder_1_out6), .WR1(decoder_2_out6), .CLK(CLK), .Q(sn74172_register_7_q));
  SN74172_Register sn74172_register_8 (
    .D0(D0), .D1(D1), .WR0(decoder_1_out7), .WR1(decoder_2_out7), .CLK(CLK), .Q(sn74172_register_8_q));
  Multiplexer #(.select(3), .width(16)) multiplexer_1 (
    .in0(sn74172_register_1_q), .in1(sn74172_register_2_q), .in2(sn74172_register_3_q),
    .in3(sn74172_register_4_q), .in4(sn74172_register_5_q), .in5(sn74172_register_6_q),
    .in6(sn74172_register_7_q), .in7(sn74172_register_8_q), .out(Q1), .sel(WR1), .en(not_4_out));
  Multiplexer #(.select(3), .width(16)) multiplexer_2 (
    .in0(sn74172_register_1_q), .in1(sn74172_register_2_q), .in2(sn74172_register_3_q),
    .in3(sn74172_register_4_q), .in4(sn74172_register_5_q), .in5(sn74172_register_6_q),
    .in6(sn74172_register_7_q), .in7(sn74172_register_8_q), .out(Q0), .sel(R0), .en(not_3_out));
endmodule

module Immediate (
  input  invert,
  input  decr,
  input  [3:0] \bit ,
  output [15:0] out_4
);

  wire not_1_out, not_2_out;
  wire [15:0] decoder_1_out0, subtractor_1_out;

  not not_1 (not_1_out, decr);
  Decoder #(.select(4), .disabled(0), .enable("false")) decoder_1 (
    .out0(decoder_1_out0[0]), .out1(decoder_1_out0[1]), .out2(decoder_1_out0[2]), .out3(decoder_1_out0[3]),
    .out4(decoder_1_out0[4]), .out5(decoder_1_out0[5]), .out6(decoder_1_out0[6]), .out7(decoder_1_out0[7]),
    .out8(decoder_1_out0[8]), .out9(decoder_1_out0[9]), .out10(decoder_1_out0[10]),
    .out11(decoder_1_out0[11]), .out12(decoder_1_out0[12]), .out13(decoder_1_out0[13]),
    .out14(decoder_1_out0[14]), .out15(decoder_1_out0[15]), .sel(\bit ));
  Subtractor #(.width(16)) subtractor_1 (
    .a(decoder_1_out0), .b({16{1'b0}}), .out(subtractor_1_out), .bin(not_1_out));  // open: bout
  not not_2 (not_2_out, invert);
  assign out_4 = not_2_out ? subtractor_1_out : 16'bz;  // Controlled_Buffer controlled_buffer_1
  assign out_4 = invert ? ~subtractor_1_out : 16'bz;  // Controlled_Inverter controlled_inverter_1
endmodule

module TLB_Cell (
  input  [3:0] INDEX,
  input  RST,
  input  CLK,
  input  WR,
  input  RD,
  input  WBANK,
  input  WFLAG,
  input  PREVIOUS,
  input  [15:0] MATCH,
  input  [15:0] DATA,
  output [3:0] INDEX_2,
  output RST_2,
  output CLK_2,
  output WR_2,
  output RD_2,
  output WBANK_2,
  output WFLAG_2,
  output ACTIVE,
  output [15:0] MATCH_2,
  output [15:0] DATA_2,
  output [11:0] RESULT
);

  wire and_1_out, and_2_out, and_3_out, and_4_out, comparator_1_eq, comparator_2_eq, not_1_out, not_2_out,
       not_3_out, or_1_out, or_2_out;
  wire [15:0] register_1_q, register_2_q;

  Adder #(.width(4)) adder_1 (.a(INDEX), .b(4'b1111), .out(INDEX_2));  // open: cin, cout
  Comparator #(.width(4)) comparator_1 (.a(INDEX), .b(4'b1111), .eq(comparator_1_eq));  // open: gt, lt
  and and_1 (and_1_out, comparator_1_eq, WBANK);
  and and_2 (and_2_out, comparator_1_eq, WFLAG);
  not not_1 (not_1_out, RD);
  Register #(.width(16)) register_1 (.D(DATA), .en(and_1_out), .Q(register_1_q), .clk(CLK), .clr(RST));
  Register #(.width(16)) register_2 (.D(DATA), .en(and_2_out), .Q(register_2_q), .clk(CLK), .clr(RST));
  not not_2 (not_2_out, WR);
  Comparator #(.width(16)) comparator_2 (.a(MATCH), .b(register_1_q), .eq(comparator_2_eq));  // open: gt, lt
  and and_3 (and_3_out, comparator_2_eq, register_2_q[2]);
  or or_1 (or_1_out, not_2_out, register_2_q[0]);
  or or_2 (or_2_out, not_1_out, register_2_q[1]);
  not not_3 (not_3_out, PREVIOUS);
  and and_4 (and_4_out, not_3_out, and_3_out, or_1_out, or_2_out);
  or or_3 (ACTIVE, PREVIOUS, and_4_out);
  assign RESULT = and_4_out ? register_2_q[15:4] : 12'bz;  // Controlled_Buffer controlled_buffer_1

  assign CLK_2 = CLK;
  assign DATA_2 = DATA;
  assign MATCH_2 = MATCH;
  assign RD_2 = RD;
  assign RST_2 = RST;
  assign WBANK_2 = WBANK;
  assign WFLAG_2 = WFLAG;
  assign WR_2 = WR;

  // Notes on the sheet:
  //   PREVIOUS: pull=down
endmodule

module TLB_Matrix (
  input  [15:0] DATA,
  input  [3:0] PID,
  input  [23:0] ADDR,
  input  [1:0] TLB_WRITE,
  input  BYPASS,
  input  RST,
  input  CLK,
  input  WR,
  input  RD,
  output [23:0] out_10,
  output ACTIVE
);

  wire decoder_1_out1, decoder_1_out2, decoder_1_out3, tlb_cell_1_active, tlb_cell_1_clk_2, tlb_cell_1_rd_2,
       tlb_cell_1_rst_2, tlb_cell_1_wbank_2, tlb_cell_1_wflag_2, tlb_cell_1_wr_2, tlb_cell_2_active,
       tlb_cell_2_clk_2, tlb_cell_2_rd_2, tlb_cell_2_rst_2, tlb_cell_2_wbank_2, tlb_cell_2_wflag_2,
       tlb_cell_2_wr_2, tlb_cell_3_active, tlb_cell_3_clk_2, tlb_cell_3_rd_2, tlb_cell_3_rst_2,
       tlb_cell_3_wbank_2, tlb_cell_3_wflag_2, tlb_cell_3_wr_2, tlb_cell_4_active, tlb_cell_4_clk_2,
       tlb_cell_4_rd_2, tlb_cell_4_rst_2, tlb_cell_4_wbank_2, tlb_cell_4_wflag_2, tlb_cell_4_wr_2,
       tlb_cell_5_active, tlb_cell_5_clk_2, tlb_cell_5_rd_2, tlb_cell_5_rst_2, tlb_cell_5_wbank_2,
       tlb_cell_5_wflag_2, tlb_cell_5_wr_2, tlb_cell_6_active, tlb_cell_6_clk_2, tlb_cell_6_rd_2,
       tlb_cell_6_rst_2, tlb_cell_6_wbank_2, tlb_cell_6_wflag_2, tlb_cell_6_wr_2, tlb_cell_7_active,
       tlb_cell_7_clk_2, tlb_cell_7_rd_2, tlb_cell_7_rst_2, tlb_cell_7_wbank_2, tlb_cell_7_wflag_2,
       tlb_cell_7_wr_2, tlb_cell_8_active, tlb_cell_8_clk_2, tlb_cell_8_rd_2, tlb_cell_8_rst_2,
       tlb_cell_8_wbank_2, tlb_cell_8_wflag_2, tlb_cell_8_wr_2, tlb_cell_9_active, tlb_cell_9_clk_2,
       tlb_cell_9_rd_2, tlb_cell_9_rst_2, tlb_cell_9_wbank_2, tlb_cell_9_wflag_2, tlb_cell_9_wr_2,
       tlb_cell_10_active, tlb_cell_10_clk_2, tlb_cell_10_rd_2, tlb_cell_10_rst_2, tlb_cell_10_wbank_2,
       tlb_cell_10_wflag_2, tlb_cell_10_wr_2, tlb_cell_11_active, tlb_cell_11_clk_2, tlb_cell_11_rd_2,
       tlb_cell_11_rst_2, tlb_cell_11_wbank_2, tlb_cell_11_wflag_2, tlb_cell_11_wr_2, tlb_cell_12_active,
       tlb_cell_12_clk_2, tlb_cell_12_rd_2, tlb_cell_12_rst_2, tlb_cell_12_wbank_2, tlb_cell_12_wflag_2,
       tlb_cell_12_wr_2, tlb_cell_13_active, tlb_cell_13_clk_2, tlb_cell_13_rd_2, tlb_cell_13_rst_2,
       tlb_cell_13_wbank_2, tlb_cell_13_wflag_2, tlb_cell_13_wr_2, tlb_cell_14_active, tlb_cell_14_clk_2,
       tlb_cell_14_rd_2, tlb_cell_14_rst_2, tlb_cell_14_wbank_2, tlb_cell_14_wflag_2, tlb_cell_14_wr_2,
       tlb_cell_15_active, tlb_cell_15_clk_2, tlb_cell_15_rd_2, tlb_cell_15_rst_2, tlb_cell_15_wbank_2,
       tlb_cell_15_wflag_2, tlb_cell_15_wr_2, tlb_cell_16_wflag_2;
  wire [3:0] register_1_q, tlb_cell_1_index_2, tlb_cell_2_index_2, tlb_cell_3_index_2, tlb_cell_4_index_2,
       tlb_cell_5_index_2, tlb_cell_6_index_2, tlb_cell_7_index_2, tlb_cell_8_index_2, tlb_cell_9_index_2,
       tlb_cell_10_index_2, tlb_cell_11_index_2, tlb_cell_12_index_2, tlb_cell_13_index_2,
       tlb_cell_14_index_2, tlb_cell_15_index_2;
  wire [11:0] tlb_cell_1_result;
  wire [15:0] tlb_cell_1_data_2, tlb_cell_1_match_2, tlb_cell_2_data_2, tlb_cell_2_match_2,
       tlb_cell_3_data_2, tlb_cell_3_match_2, tlb_cell_4_data_2, tlb_cell_4_match_2, tlb_cell_5_data_2,
       tlb_cell_5_match_2, tlb_cell_6_data_2, tlb_cell_6_match_2, tlb_cell_7_data_2, tlb_cell_7_match_2,
       tlb_cell_8_data_2, tlb_cell_8_match_2, tlb_cell_9_data_2, tlb_cell_9_match_2, tlb_cell_10_data_2,
       tlb_cell_10_match_2, tlb_cell_11_data_2, tlb_cell_11_match_2, tlb_cell_12_data_2, tlb_cell_12_match_2,
       tlb_cell_13_data_2, tlb_cell_13_match_2, tlb_cell_14_data_2, tlb_cell_14_match_2, tlb_cell_15_data_2,
       tlb_cell_15_match_2;

  Decoder #(.select(2), .enable("false")) decoder_1 (
    .out1(decoder_1_out1), .out2(decoder_1_out2), .out3(decoder_1_out3), .sel(TLB_WRITE));  // open: out0
  Register #(.width(4)) register_1 (.D(DATA[3:0]), .en(decoder_1_out1), .Q(register_1_q), .clk(CLK), .clr(RST));
  TLB_Cell tlb_cell_1 (
    .INDEX(register_1_q), .RST(RST), .CLK(CLK), .WR(WR), .RD(RD), .WBANK(decoder_1_out2),
    .WFLAG(decoder_1_out3), .MATCH({ADDR[23:12], PID}), .DATA(DATA), .INDEX_2(tlb_cell_1_index_2),
    .RST_2(tlb_cell_1_rst_2), .CLK_2(tlb_cell_1_clk_2), .WR_2(tlb_cell_1_wr_2), .RD_2(tlb_cell_1_rd_2),
    .WBANK_2(tlb_cell_1_wbank_2), .WFLAG_2(tlb_cell_1_wflag_2), .ACTIVE(tlb_cell_1_active),
    .MATCH_2(tlb_cell_1_match_2), .DATA_2(tlb_cell_1_data_2), .RESULT(tlb_cell_1_result));  // open: PREVIOUS
  TLB_Cell tlb_cell_2 (
    .INDEX(tlb_cell_1_index_2), .RST(tlb_cell_1_rst_2), .CLK(tlb_cell_1_clk_2), .WR(tlb_cell_1_wr_2),
    .RD(tlb_cell_1_rd_2), .WBANK(tlb_cell_1_wbank_2), .WFLAG(tlb_cell_1_wflag_2),
    .PREVIOUS(tlb_cell_1_active), .MATCH(tlb_cell_1_match_2), .DATA(tlb_cell_1_data_2),
    .INDEX_2(tlb_cell_2_index_2), .RST_2(tlb_cell_2_rst_2), .CLK_2(tlb_cell_2_clk_2), .WR_2(tlb_cell_2_wr_2),
    .RD_2(tlb_cell_2_rd_2), .WBANK_2(tlb_cell_2_wbank_2), .WFLAG_2(tlb_cell_2_wflag_2),
    .ACTIVE(tlb_cell_2_active), .MATCH_2(tlb_cell_2_match_2), .DATA_2(tlb_cell_2_data_2),
    .RESULT(tlb_cell_1_result));
  TLB_Cell tlb_cell_3 (
    .INDEX(tlb_cell_2_index_2), .RST(tlb_cell_2_rst_2), .CLK(tlb_cell_2_clk_2), .WR(tlb_cell_2_wr_2),
    .RD(tlb_cell_2_rd_2), .WBANK(tlb_cell_2_wbank_2), .WFLAG(tlb_cell_2_wflag_2),
    .PREVIOUS(tlb_cell_2_active), .MATCH(tlb_cell_2_match_2), .DATA(tlb_cell_2_data_2),
    .INDEX_2(tlb_cell_3_index_2), .RST_2(tlb_cell_3_rst_2), .CLK_2(tlb_cell_3_clk_2), .WR_2(tlb_cell_3_wr_2),
    .RD_2(tlb_cell_3_rd_2), .WBANK_2(tlb_cell_3_wbank_2), .WFLAG_2(tlb_cell_3_wflag_2),
    .ACTIVE(tlb_cell_3_active), .MATCH_2(tlb_cell_3_match_2), .DATA_2(tlb_cell_3_data_2),
    .RESULT(tlb_cell_1_result));
  TLB_Cell tlb_cell_4 (
    .INDEX(tlb_cell_3_index_2), .RST(tlb_cell_3_rst_2), .CLK(tlb_cell_3_clk_2), .WR(tlb_cell_3_wr_2),
    .RD(tlb_cell_3_rd_2), .WBANK(tlb_cell_3_wbank_2), .WFLAG(tlb_cell_3_wflag_2),
    .PREVIOUS(tlb_cell_3_active), .MATCH(tlb_cell_3_match_2), .DATA(tlb_cell_3_data_2),
    .INDEX_2(tlb_cell_4_index_2), .RST_2(tlb_cell_4_rst_2), .CLK_2(tlb_cell_4_clk_2), .WR_2(tlb_cell_4_wr_2),
    .RD_2(tlb_cell_4_rd_2), .WBANK_2(tlb_cell_4_wbank_2), .WFLAG_2(tlb_cell_4_wflag_2),
    .ACTIVE(tlb_cell_4_active), .MATCH_2(tlb_cell_4_match_2), .DATA_2(tlb_cell_4_data_2),
    .RESULT(tlb_cell_1_result));
  TLB_Cell tlb_cell_5 (
    .INDEX(tlb_cell_6_index_2), .RST(tlb_cell_6_rst_2), .CLK(tlb_cell_6_clk_2), .WR(tlb_cell_6_wr_2),
    .RD(tlb_cell_6_rd_2), .WBANK(tlb_cell_6_wbank_2), .WFLAG(tlb_cell_6_wflag_2),
    .PREVIOUS(tlb_cell_6_active), .MATCH(tlb_cell_6_match_2), .DATA(tlb_cell_6_data_2),
    .INDEX_2(tlb_cell_5_index_2), .RST_2(tlb_cell_5_rst_2), .CLK_2(tlb_cell_5_clk_2), .WR_2(tlb_cell_5_wr_2),
    .RD_2(tlb_cell_5_rd_2), .WBANK_2(tlb_cell_5_wbank_2), .WFLAG_2(tlb_cell_5_wflag_2),
    .ACTIVE(tlb_cell_5_active), .MATCH_2(tlb_cell_5_match_2), .DATA_2(tlb_cell_5_data_2),
    .RESULT(tlb_cell_1_result));
  TLB_Cell tlb_cell_6 (
    .INDEX(tlb_cell_4_index_2), .RST(tlb_cell_4_rst_2), .CLK(tlb_cell_4_clk_2), .WR(tlb_cell_4_wr_2),
    .RD(tlb_cell_4_rd_2), .WBANK(tlb_cell_4_wbank_2), .WFLAG(tlb_cell_4_wflag_2),
    .PREVIOUS(tlb_cell_4_active), .MATCH(tlb_cell_4_match_2), .DATA(tlb_cell_4_data_2),
    .INDEX_2(tlb_cell_6_index_2), .RST_2(tlb_cell_6_rst_2), .CLK_2(tlb_cell_6_clk_2), .WR_2(tlb_cell_6_wr_2),
    .RD_2(tlb_cell_6_rd_2), .WBANK_2(tlb_cell_6_wbank_2), .WFLAG_2(tlb_cell_6_wflag_2),
    .ACTIVE(tlb_cell_6_active), .MATCH_2(tlb_cell_6_match_2), .DATA_2(tlb_cell_6_data_2),
    .RESULT(tlb_cell_1_result));
  TLB_Cell tlb_cell_7 (
    .INDEX(tlb_cell_8_index_2), .RST(tlb_cell_8_rst_2), .CLK(tlb_cell_8_clk_2), .WR(tlb_cell_8_wr_2),
    .RD(tlb_cell_8_rd_2), .WBANK(tlb_cell_8_wbank_2), .WFLAG(tlb_cell_8_wflag_2),
    .PREVIOUS(tlb_cell_8_active), .MATCH(tlb_cell_8_match_2), .DATA(tlb_cell_8_data_2),
    .INDEX_2(tlb_cell_7_index_2), .RST_2(tlb_cell_7_rst_2), .CLK_2(tlb_cell_7_clk_2), .WR_2(tlb_cell_7_wr_2),
    .RD_2(tlb_cell_7_rd_2), .WBANK_2(tlb_cell_7_wbank_2), .WFLAG_2(tlb_cell_7_wflag_2),
    .ACTIVE(tlb_cell_7_active), .MATCH_2(tlb_cell_7_match_2), .DATA_2(tlb_cell_7_data_2));  // open: RESULT
  TLB_Cell tlb_cell_8 (
    .INDEX(tlb_cell_5_index_2), .RST(tlb_cell_5_rst_2), .CLK(tlb_cell_5_clk_2), .WR(tlb_cell_5_wr_2),
    .RD(tlb_cell_5_rd_2), .WBANK(tlb_cell_5_wbank_2), .WFLAG(tlb_cell_5_wflag_2),
    .PREVIOUS(tlb_cell_5_active), .MATCH(tlb_cell_5_match_2), .DATA(tlb_cell_5_data_2),
    .INDEX_2(tlb_cell_8_index_2), .RST_2(tlb_cell_8_rst_2), .CLK_2(tlb_cell_8_clk_2), .WR_2(tlb_cell_8_wr_2),
    .RD_2(tlb_cell_8_rd_2), .WBANK_2(tlb_cell_8_wbank_2), .WFLAG_2(tlb_cell_8_wflag_2),
    .ACTIVE(tlb_cell_8_active), .MATCH_2(tlb_cell_8_match_2), .DATA_2(tlb_cell_8_data_2),
    .RESULT(tlb_cell_1_result));
  TLB_Cell tlb_cell_9 (
    .INDEX(tlb_cell_7_index_2), .RST(tlb_cell_7_rst_2), .CLK(tlb_cell_7_clk_2), .WR(tlb_cell_7_wr_2),
    .RD(tlb_cell_7_rd_2), .WBANK(tlb_cell_7_wbank_2), .WFLAG(tlb_cell_7_wflag_2),
    .PREVIOUS(tlb_cell_7_active), .MATCH(tlb_cell_7_match_2), .DATA(tlb_cell_7_data_2),
    .INDEX_2(tlb_cell_9_index_2), .RST_2(tlb_cell_9_rst_2), .CLK_2(tlb_cell_9_clk_2), .WR_2(tlb_cell_9_wr_2),
    .RD_2(tlb_cell_9_rd_2), .WBANK_2(tlb_cell_9_wbank_2), .WFLAG_2(tlb_cell_9_wflag_2),
    .ACTIVE(tlb_cell_9_active), .MATCH_2(tlb_cell_9_match_2), .DATA_2(tlb_cell_9_data_2),
    .RESULT(tlb_cell_1_result));
  TLB_Cell tlb_cell_10 (
    .INDEX(tlb_cell_9_index_2), .RST(tlb_cell_9_rst_2), .CLK(tlb_cell_9_clk_2), .WR(tlb_cell_9_wr_2),
    .RD(tlb_cell_9_rd_2), .WBANK(tlb_cell_9_wbank_2), .WFLAG(tlb_cell_9_wflag_2),
    .PREVIOUS(tlb_cell_9_active), .MATCH(tlb_cell_9_match_2), .DATA(tlb_cell_9_data_2),
    .INDEX_2(tlb_cell_10_index_2), .RST_2(tlb_cell_10_rst_2), .CLK_2(tlb_cell_10_clk_2),
    .WR_2(tlb_cell_10_wr_2), .RD_2(tlb_cell_10_rd_2), .WBANK_2(tlb_cell_10_wbank_2),
    .WFLAG_2(tlb_cell_10_wflag_2), .ACTIVE(tlb_cell_10_active), .MATCH_2(tlb_cell_10_match_2),
    .DATA_2(tlb_cell_10_data_2), .RESULT(tlb_cell_1_result));
  TLB_Cell tlb_cell_11 (
    .INDEX(tlb_cell_10_index_2), .RST(tlb_cell_10_rst_2), .CLK(tlb_cell_10_clk_2), .WR(tlb_cell_10_wr_2),
    .RD(tlb_cell_10_rd_2), .WBANK(tlb_cell_10_wbank_2), .WFLAG(tlb_cell_10_wflag_2),
    .PREVIOUS(tlb_cell_10_active), .MATCH(tlb_cell_10_match_2), .DATA(tlb_cell_10_data_2),
    .INDEX_2(tlb_cell_11_index_2), .RST_2(tlb_cell_11_rst_2), .CLK_2(tlb_cell_11_clk_2),
    .WR_2(tlb_cell_11_wr_2), .RD_2(tlb_cell_11_rd_2), .WBANK_2(tlb_cell_11_wbank_2),
    .WFLAG_2(tlb_cell_11_wflag_2), .ACTIVE(tlb_cell_11_active), .MATCH_2(tlb_cell_11_match_2),
    .DATA_2(tlb_cell_11_data_2), .RESULT(tlb_cell_1_result));
  TLB_Cell tlb_cell_12 (
    .INDEX(tlb_cell_11_index_2), .RST(tlb_cell_11_rst_2), .CLK(tlb_cell_11_clk_2), .WR(tlb_cell_11_wr_2),
    .RD(tlb_cell_11_rd_2), .WBANK(tlb_cell_11_wbank_2), .WFLAG(tlb_cell_11_wflag_2),
    .PREVIOUS(tlb_cell_11_active), .MATCH(tlb_cell_11_match_2), .DATA(tlb_cell_11_data_2),
    .INDEX_2(tlb_cell_12_index_2), .RST_2(tlb_cell_12_rst_2), .CLK_2(tlb_cell_12_clk_2),
    .WR_2(tlb_cell_12_wr_2), .RD_2(tlb_cell_12_rd_2), .WBANK_2(tlb_cell_12_wbank_2),
    .WFLAG_2(tlb_cell_12_wflag_2), .ACTIVE(tlb_cell_12_active), .MATCH_2(tlb_cell_12_match_2),
    .DATA_2(tlb_cell_12_data_2), .RESULT(tlb_cell_1_result));
  TLB_Cell tlb_cell_13 (
    .INDEX(tlb_cell_12_index_2), .RST(tlb_cell_12_rst_2), .CLK(tlb_cell_12_clk_2), .WR(tlb_cell_12_wr_2),
    .RD(tlb_cell_12_rd_2), .WBANK(tlb_cell_12_wbank_2), .WFLAG(tlb_cell_12_wflag_2),
    .PREVIOUS(tlb_cell_12_active), .MATCH(tlb_cell_12_match_2), .DATA(tlb_cell_12_data_2),
    .INDEX_2(tlb_cell_13_index_2), .RST_2(tlb_cell_13_rst_2), .CLK_2(tlb_cell_13_clk_2),
    .WR_2(tlb_cell_13_wr_2), .RD_2(tlb_cell_13_rd_2), .WBANK_2(tlb_cell_13_wbank_2),
    .WFLAG_2(tlb_cell_13_wflag_2), .ACTIVE(tlb_cell_13_active), .MATCH_2(tlb_cell_13_match_2),
    .DATA_2(tlb_cell_13_data_2), .RESULT(tlb_cell_1_result));
  TLB_Cell tlb_cell_14 (
    .INDEX(tlb_cell_13_index_2), .RST(tlb_cell_13_rst_2), .CLK(tlb_cell_13_clk_2), .WR(tlb_cell_13_wr_2),
    .RD(tlb_cell_13_rd_2), .WBANK(tlb_cell_13_wbank_2), .WFLAG(tlb_cell_13_wflag_2),
    .PREVIOUS(tlb_cell_13_active), .MATCH(tlb_cell_13_match_2), .DATA(tlb_cell_13_data_2),
    .INDEX_2(tlb_cell_14_index_2), .RST_2(tlb_cell_14_rst_2), .CLK_2(tlb_cell_14_clk_2),
    .WR_2(tlb_cell_14_wr_2), .RD_2(tlb_cell_14_rd_2), .WBANK_2(tlb_cell_14_wbank_2),
    .WFLAG_2(tlb_cell_14_wflag_2), .ACTIVE(tlb_cell_14_active), .MATCH_2(tlb_cell_14_match_2),
    .DATA_2(tlb_cell_14_data_2), .RESULT(tlb_cell_1_result));
  TLB_Cell tlb_cell_15 (
    .INDEX(tlb_cell_14_index_2), .RST(tlb_cell_14_rst_2), .CLK(tlb_cell_14_clk_2), .WR(tlb_cell_14_wr_2),
    .RD(tlb_cell_14_rd_2), .WBANK(tlb_cell_14_wbank_2), .WFLAG(tlb_cell_14_wflag_2),
    .PREVIOUS(tlb_cell_14_active), .MATCH(tlb_cell_14_match_2), .DATA(tlb_cell_14_data_2),
    .INDEX_2(tlb_cell_15_index_2), .RST_2(tlb_cell_15_rst_2), .CLK_2(tlb_cell_15_clk_2),
    .WR_2(tlb_cell_15_wr_2), .RD_2(tlb_cell_15_rd_2), .WBANK_2(tlb_cell_15_wbank_2),
    .WFLAG_2(tlb_cell_15_wflag_2), .ACTIVE(tlb_cell_15_active), .MATCH_2(tlb_cell_15_match_2),
    .DATA_2(tlb_cell_15_data_2), .RESULT(tlb_cell_1_result));
  TLB_Cell tlb_cell_16 (
    .INDEX(tlb_cell_15_index_2), .RST(tlb_cell_15_rst_2), .CLK(tlb_cell_15_clk_2), .WR(tlb_cell_15_wr_2),
    .RD(tlb_cell_15_rd_2), .WBANK(tlb_cell_15_wbank_2), .WFLAG(tlb_cell_15_wflag_2),
    .PREVIOUS(tlb_cell_15_active), .MATCH(tlb_cell_15_match_2), .DATA(tlb_cell_15_data_2),
    .WFLAG_2(tlb_cell_16_wflag_2));  // open: INDEX_2, RST_2, CLK_2, WR_2, RD_2, WBANK_2, ACTIVE, MATCH_2, DATA_2, RESULT
  Multiplexer #(.width(12), .enable("false")) multiplexer_1 (
    .in0(tlb_cell_1_result), .in1(ADDR[23:12]), .out(out_10[23:12]), .sel(BYPASS));
  or or_1 (ACTIVE, tlb_cell_16_wflag_2, BYPASS);

  assign out_10[11:0] = ADDR[11:0];
endmodule
